# Fritzing sketch wiring ph,tds,turbidity (saved by Fritzing 0.9.3b)

parts:
  A1 = ESP32 devkit 38p expansion board
  esp1 = ESP32 DevKitc V4  # not connected
  M2 = ph-4502c [package=THT]
  A2 = tds-sensor-meter-v1.0_1
  A3 = TS-300B interface
  A4 = TS 300B sensor
  Part1 = ADS1115
  J1 = rounded female pin header, 1 pin [form="♀ (female rounded)"]  # not connected
  J2 = female pin header, 1 pin [form="♀ (female)"]

nets:
  N1: A1.Pin_4, A3.Pin_2
  N2: A1.Pin_5, A2.pin1
  N3: A1.Pin_17, A1.Pin_56, A1.Pin_57, M2.pin6, A3.Pin_4
  N4: A1.Pin_54, A1.Pin_144, M2.pin4, M2.pin5, A2.pin3
  N5: A1.Pin_58, A1.Pin_59, A2.pin2, Part1.VDD
  N6: A1.Pin_174, Part1.SDA
  N7: A1.Pin_177, Part1.SCL
  N8: M2.pin3, Part1.A0
  N9: A3.Pin_1, A3.Pin_8, J2.pin1
  N10: A3.Pin_5, A4.Pin_3
  N11: A3.Pin_6, A4.Pin_2
  N12: A3.Pin_7, A4.Pin_1

custom parts:
  ESP32 devkit 38p expansion board: Upgraded ESP32 38P Development ESP32-DevKitC-32 ESP-WROOM-32 Expansion Board.
  ESP32 DevKitc V4: ESP32-DevKitC board with ESP32-WROOM-32 module. ESP32-DevKitC V4 is a small-sized ESP32-based development board produced by Espressif. Most of the pins on the ESP module are broken out to the pin headers on the board. The pins D0, D1, D2, D3, CMD and CLK are used internally for communication between ESP32 and SPI flash memory. They are grouped on both sides near the USB connector. Avoid using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
  ph-4502c: ph-4502c PH Meter.
  : TDS Meter V1.0 Development Board Water Meter Filter Measuring Water Sensor Module.
  TS-300B interface: TS-300B interface.
  TS 300B sensor: TS 300B water turbidity sensor.
  ADS1115: ADC ADS1115
